// Logisim project shiftleft32.circ as structural Verilog: 1 circuit, main circuit main
module main (
  input  [31:0] B,
  input  Cin,
  input  [4:0] Sa,
  output [31:0] C
);

  wire multiplexer_1_out, multiplexer_2_out, multiplexer_3_out, multiplexer_4_out, multiplexer_5_out,
       multiplexer_6_out, multiplexer_7_out, multiplexer_8_out, multiplexer_9_out, multiplexer_10_out,
       multiplexer_13_out, multiplexer_14_out, multiplexer_15_out, multiplexer_16_out, multiplexer_17_out,
       multiplexer_18_out, multiplexer_21_out, multiplexer_22_out, multiplexer_23_out, multiplexer_24_out,
       multiplexer_25_out, multiplexer_26_out, multiplexer_27_out, multiplexer_29_out, multiplexer_30_out,
       multiplexer_31_out, multiplexer_32_out, multiplexer_33_out, multiplexer_34_out, multiplexer_37_out,
       multiplexer_38_out, multiplexer_39_out, multiplexer_40_out, multiplexer_41_out, multiplexer_42_out,
       multiplexer_43_out, multiplexer_45_out, multiplexer_46_out, multiplexer_47_out, multiplexer_48_out,
       multiplexer_49_out, multiplexer_50_out, multiplexer_53_out, multiplexer_54_out, multiplexer_55_out,
       multiplexer_56_out, multiplexer_57_out, multiplexer_58_out, multiplexer_61_out, multiplexer_62_out,
       multiplexer_63_out, multiplexer_64_out, multiplexer_65_out, multiplexer_66_out, multiplexer_67_out,
       multiplexer_69_out, multiplexer_70_out, multiplexer_71_out, multiplexer_72_out, multiplexer_73_out,
       multiplexer_74_out, multiplexer_77_out, multiplexer_78_out, multiplexer_79_out, multiplexer_80_out,
       multiplexer_81_out, multiplexer_82_out, multiplexer_83_out, multiplexer_85_out, multiplexer_86_out,
       multiplexer_87_out, multiplexer_88_out, multiplexer_89_out, multiplexer_90_out, multiplexer_93_out,
       multiplexer_94_out, multiplexer_95_out, multiplexer_96_out, multiplexer_97_out, multiplexer_98_out,
       multiplexer_101_out, multiplexer_102_out, multiplexer_103_out, multiplexer_104_out,
       multiplexer_105_out, multiplexer_106_out, multiplexer_107_out, multiplexer_109_out,
       multiplexer_110_out, multiplexer_111_out, multiplexer_112_out, multiplexer_113_out,
       multiplexer_114_out, multiplexer_117_out, multiplexer_118_out, multiplexer_119_out,
       multiplexer_120_out, multiplexer_121_out, multiplexer_122_out, multiplexer_123_out,
       multiplexer_125_out, multiplexer_126_out, multiplexer_127_out, multiplexer_128_out,
       multiplexer_129_out, multiplexer_130_out, multiplexer_133_out, multiplexer_134_out,
       multiplexer_135_out, multiplexer_136_out, multiplexer_137_out, multiplexer_138_out,
       multiplexer_141_out, multiplexer_142_out, multiplexer_143_out, multiplexer_144_out,
       multiplexer_145_out, multiplexer_146_out, multiplexer_147_out, multiplexer_149_out,
       multiplexer_150_out, multiplexer_151_out, multiplexer_152_out, multiplexer_153_out,
       multiplexer_154_out, multiplexer_157_out, multiplexer_158_out, multiplexer_159_out;

  Multiplexer #(.enable("false")) multiplexer_1 (.in0(B[31]), .in1(B[15]), .out(multiplexer_1_out), .sel(Sa[4]));
  Multiplexer #(.enable("false")) multiplexer_2 (
    .in0(multiplexer_1_out), .in1(multiplexer_37_out), .out(multiplexer_2_out), .sel(Sa[3]));
  Multiplexer #(.enable("false")) multiplexer_3 (
    .in0(multiplexer_2_out), .in1(multiplexer_23_out), .out(multiplexer_3_out), .sel(Sa[2]));
  Multiplexer #(.enable("false")) multiplexer_4 (
    .in0(multiplexer_3_out), .in1(multiplexer_16_out), .out(multiplexer_4_out), .sel(Sa[1]));
  Multiplexer #(.enable("false")) multiplexer_5 (.in0(B[29]), .in1(B[13]), .out(multiplexer_5_out), .sel(Sa[4]));
  Multiplexer #(.enable("false")) multiplexer_6 (.in0(B[30]), .in1(B[14]), .out(multiplexer_6_out), .sel(Sa[4]));
  Multiplexer #(.enable("false")) multiplexer_7 (
    .in0(multiplexer_5_out), .in1(multiplexer_45_out), .out(multiplexer_7_out), .sel(Sa[3]));
  Multiplexer #(.enable("false")) multiplexer_8 (
    .in0(multiplexer_6_out), .in1(multiplexer_46_out), .out(multiplexer_8_out), .sel(Sa[3]));
  Multiplexer #(.enable("false")) multiplexer_9 (
    .in0(multiplexer_8_out), .in1(multiplexer_24_out), .out(multiplexer_9_out), .sel(Sa[2]));
  Multiplexer #(.enable("false")) multiplexer_10 (
    .in0(multiplexer_9_out), .in1(multiplexer_15_out), .out(multiplexer_10_out), .sel(Sa[1]));
  Multiplexer #(.enable("false")) multiplexer_11 (
    .in0(multiplexer_4_out), .in1(multiplexer_10_out), .out(C[31]), .sel(Sa[0]));
  Multiplexer #(.enable("false")) multiplexer_12 (
    .in0(multiplexer_10_out), .in1(multiplexer_17_out), .out(C[30]), .sel(Sa[0]));
  Multiplexer #(.enable("false")) multiplexer_13 (.in0(B[28]), .in1(B[12]), .out(multiplexer_13_out), .sel(Sa[4]));
  Multiplexer #(.enable("false")) multiplexer_14 (
    .in0(multiplexer_13_out), .in1(multiplexer_53_out), .out(multiplexer_14_out), .sel(Sa[3]));
  Multiplexer #(.enable("false")) multiplexer_15 (
    .in0(multiplexer_14_out), .in1(multiplexer_38_out), .out(multiplexer_15_out), .sel(Sa[2]));
  Multiplexer #(.enable("false")) multiplexer_16 (
    .in0(multiplexer_7_out), .in1(multiplexer_31_out), .out(multiplexer_16_out), .sel(Sa[2]));
  Multiplexer #(.enable("false")) multiplexer_17 (
    .in0(multiplexer_16_out), .in1(multiplexer_26_out), .out(multiplexer_17_out), .sel(Sa[1]));
  Multiplexer #(.enable("false")) multiplexer_18 (
    .in0(multiplexer_15_out), .in1(multiplexer_25_out), .out(multiplexer_18_out), .sel(Sa[1]));
  Multiplexer #(.enable("false")) multiplexer_19 (
    .in0(multiplexer_17_out), .in1(multiplexer_18_out), .out(C[29]), .sel(Sa[0]));
  Multiplexer #(.enable("false")) multiplexer_20 (
    .in0(multiplexer_18_out), .in1(multiplexer_27_out), .out(C[28]), .sel(Sa[0]));
  Multiplexer #(.enable("false")) multiplexer_21 (.in0(B[27]), .in1(B[11]), .out(multiplexer_21_out), .sel(Sa[4]));
  Multiplexer #(.enable("false")) multiplexer_22 (.in0(B[26]), .in1(B[10]), .out(multiplexer_22_out), .sel(Sa[4]));
  Multiplexer #(.enable("false")) multiplexer_23 (
    .in0(multiplexer_21_out), .in1(multiplexer_61_out), .out(multiplexer_23_out), .sel(Sa[3]));
  Multiplexer #(.enable("false")) multiplexer_24 (
    .in0(multiplexer_22_out), .in1(multiplexer_62_out), .out(multiplexer_24_out), .sel(Sa[3]));
  Multiplexer #(.enable("false")) multiplexer_25 (
    .in0(multiplexer_24_out), .in1(multiplexer_47_out), .out(multiplexer_25_out), .sel(Sa[2]));
  Multiplexer #(.enable("false")) multiplexer_26 (
    .in0(multiplexer_23_out), .in1(multiplexer_39_out), .out(multiplexer_26_out), .sel(Sa[2]));
  Multiplexer #(.enable("false")) multiplexer_27 (
    .in0(multiplexer_26_out), .in1(multiplexer_32_out), .out(multiplexer_27_out), .sel(Sa[1]));
  Multiplexer #(.enable("false")) multiplexer_28 (
    .in0(multiplexer_27_out), .in1(multiplexer_33_out), .out(C[27]), .sel(Sa[0]));
  Multiplexer #(.enable("false")) multiplexer_29 (.in0(B[24]), .in1(B[8]), .out(multiplexer_29_out), .sel(Sa[4]));
  Multiplexer #(.enable("false")) multiplexer_30 (.in0(B[25]), .in1(B[9]), .out(multiplexer_30_out), .sel(Sa[4]));
  Multiplexer #(.enable("false")) multiplexer_31 (
    .in0(multiplexer_30_out), .in1(multiplexer_69_out), .out(multiplexer_31_out), .sel(Sa[3]));
  Multiplexer #(.enable("false")) multiplexer_32 (
    .in0(multiplexer_31_out), .in1(multiplexer_48_out), .out(multiplexer_32_out), .sel(Sa[2]));
  Multiplexer #(.enable("false")) multiplexer_33 (
    .in0(multiplexer_25_out), .in1(multiplexer_41_out), .out(multiplexer_33_out), .sel(Sa[1]));
  Multiplexer #(.enable("false")) multiplexer_34 (
    .in0(multiplexer_32_out), .in1(multiplexer_40_out), .out(multiplexer_34_out), .sel(Sa[1]));
  Multiplexer #(.enable("false")) multiplexer_35 (
    .in0(multiplexer_34_out), .in1(multiplexer_43_out), .out(C[25]), .sel(Sa[0]));
  Multiplexer #(.enable("false")) multiplexer_36 (
    .in0(multiplexer_33_out), .in1(multiplexer_34_out), .out(C[26]), .sel(Sa[0]));
  Multiplexer #(.enable("false")) multiplexer_37 (.in0(B[23]), .in1(B[7]), .out(multiplexer_37_out), .sel(Sa[4]));
  Multiplexer #(.enable("false")) multiplexer_38 (
    .in0(multiplexer_29_out), .in1(multiplexer_70_out), .out(multiplexer_38_out), .sel(Sa[3]));
  Multiplexer #(.enable("false")) multiplexer_39 (
    .in0(multiplexer_37_out), .in1(multiplexer_77_out), .out(multiplexer_39_out), .sel(Sa[3]));
  Multiplexer #(.enable("false")) multiplexer_40 (
    .in0(multiplexer_39_out), .in1(multiplexer_64_out), .out(multiplexer_40_out), .sel(Sa[2]));
  Multiplexer #(.enable("false")) multiplexer_41 (
    .in0(multiplexer_38_out), .in1(multiplexer_54_out), .out(multiplexer_41_out), .sel(Sa[2]));
  Multiplexer #(.enable("false")) multiplexer_42 (
    .in0(multiplexer_40_out), .in1(multiplexer_55_out), .out(multiplexer_42_out), .sel(Sa[1]));
  Multiplexer #(.enable("false")) multiplexer_43 (
    .in0(multiplexer_41_out), .in1(multiplexer_49_out), .out(multiplexer_43_out), .sel(Sa[1]));
  Multiplexer #(.enable("false")) multiplexer_44 (
    .in0(multiplexer_43_out), .in1(multiplexer_42_out), .out(C[24]), .sel(Sa[0]));
  Multiplexer #(.enable("false")) multiplexer_45 (.in0(B[21]), .in1(B[5]), .out(multiplexer_45_out), .sel(Sa[4]));
  Multiplexer #(.enable("false")) multiplexer_46 (.in0(B[22]), .in1(B[6]), .out(multiplexer_46_out), .sel(Sa[4]));
  Multiplexer #(.enable("false")) multiplexer_47 (
    .in0(multiplexer_46_out), .in1(multiplexer_85_out), .out(multiplexer_47_out), .sel(Sa[3]));
  Multiplexer #(.enable("false")) multiplexer_48 (
    .in0(multiplexer_45_out), .in1(multiplexer_86_out), .out(multiplexer_48_out), .sel(Sa[3]));
  Multiplexer #(.enable("false")) multiplexer_49 (
    .in0(multiplexer_47_out), .in1(multiplexer_63_out), .out(multiplexer_49_out), .sel(Sa[2]));
  Multiplexer #(.enable("false")) multiplexer_50 (
    .in0(multiplexer_49_out), .in1(multiplexer_56_out), .out(multiplexer_50_out), .sel(Sa[1]));
  Multiplexer #(.enable("false")) multiplexer_51 (
    .in0(multiplexer_42_out), .in1(multiplexer_50_out), .out(C[23]), .sel(Sa[0]));
  Multiplexer #(.enable("false")) multiplexer_52 (
    .in0(multiplexer_50_out), .in1(multiplexer_57_out), .out(C[22]), .sel(Sa[0]));
  Multiplexer #(.enable("false")) multiplexer_53 (.in0(B[20]), .in1(B[4]), .out(multiplexer_53_out), .sel(Sa[4]));
  Multiplexer #(.enable("false")) multiplexer_54 (
    .in0(multiplexer_53_out), .in1(multiplexer_93_out), .out(multiplexer_54_out), .sel(Sa[3]));
  Multiplexer #(.enable("false")) multiplexer_55 (
    .in0(multiplexer_48_out), .in1(multiplexer_71_out), .out(multiplexer_55_out), .sel(Sa[2]));
  Multiplexer #(.enable("false")) multiplexer_56 (
    .in0(multiplexer_54_out), .in1(multiplexer_78_out), .out(multiplexer_56_out), .sel(Sa[2]));
  Multiplexer #(.enable("false")) multiplexer_57 (
    .in0(multiplexer_55_out), .in1(multiplexer_65_out), .out(multiplexer_57_out), .sel(Sa[1]));
  Multiplexer #(.enable("false")) multiplexer_58 (
    .in0(multiplexer_56_out), .in1(multiplexer_66_out), .out(multiplexer_58_out), .sel(Sa[1]));
  Multiplexer #(.enable("false")) multiplexer_59 (
    .in0(multiplexer_58_out), .in1(multiplexer_67_out), .out(C[20]), .sel(Sa[0]));
  Multiplexer #(.enable("false")) multiplexer_60 (
    .in0(multiplexer_57_out), .in1(multiplexer_58_out), .out(C[21]), .sel(Sa[0]));
  Multiplexer #(.enable("false")) multiplexer_61 (.in0(B[19]), .in1(B[3]), .out(multiplexer_61_out), .sel(Sa[4]));
  Multiplexer #(.enable("false")) multiplexer_62 (.in0(B[18]), .in1(B[2]), .out(multiplexer_62_out), .sel(Sa[4]));
  Multiplexer #(.enable("false")) multiplexer_63 (
    .in0(multiplexer_62_out), .in1(multiplexer_101_out), .out(multiplexer_63_out), .sel(Sa[3]));
  Multiplexer #(.enable("false")) multiplexer_64 (
    .in0(multiplexer_61_out), .in1(multiplexer_102_out), .out(multiplexer_64_out), .sel(Sa[3]));
  Multiplexer #(.enable("false")) multiplexer_65 (
    .in0(multiplexer_64_out), .in1(multiplexer_79_out), .out(multiplexer_65_out), .sel(Sa[2]));
  Multiplexer #(.enable("false")) multiplexer_66 (
    .in0(multiplexer_63_out), .in1(multiplexer_87_out), .out(multiplexer_66_out), .sel(Sa[2]));
  Multiplexer #(.enable("false")) multiplexer_67 (
    .in0(multiplexer_65_out), .in1(multiplexer_72_out), .out(multiplexer_67_out), .sel(Sa[1]));
  Multiplexer #(.enable("false")) multiplexer_68 (
    .in0(multiplexer_67_out), .in1(multiplexer_73_out), .out(C[19]), .sel(Sa[0]));
  Multiplexer #(.enable("false")) multiplexer_69 (.in0(B[17]), .in1(B[1]), .out(multiplexer_69_out), .sel(Sa[4]));
  Multiplexer #(.enable("false")) multiplexer_70 (.in0(B[16]), .in1(B[0]), .out(multiplexer_70_out), .sel(Sa[4]));
  Multiplexer #(.enable("false")) multiplexer_71 (
    .in0(multiplexer_69_out), .in1(multiplexer_110_out), .out(multiplexer_71_out), .sel(Sa[3]));
  Multiplexer #(.enable("false")) multiplexer_72 (
    .in0(multiplexer_71_out), .in1(multiplexer_88_out), .out(multiplexer_72_out), .sel(Sa[2]));
  Multiplexer #(.enable("false")) multiplexer_73 (
    .in0(multiplexer_66_out), .in1(multiplexer_80_out), .out(multiplexer_73_out), .sel(Sa[1]));
  Multiplexer #(.enable("false")) multiplexer_74 (
    .in0(multiplexer_72_out), .in1(multiplexer_81_out), .out(multiplexer_74_out), .sel(Sa[1]));
  Multiplexer #(.enable("false")) multiplexer_75 (
    .in0(multiplexer_73_out), .in1(multiplexer_74_out), .out(C[18]), .sel(Sa[0]));
  Multiplexer #(.enable("false")) multiplexer_76 (
    .in0(multiplexer_74_out), .in1(multiplexer_83_out), .out(C[17]), .sel(Sa[0]));
  Multiplexer #(.enable("false")) multiplexer_77 (.in0(B[15]), .in1(Cin), .out(multiplexer_77_out), .sel(Sa[4]));
  Multiplexer #(.enable("false")) multiplexer_78 (
    .in0(multiplexer_70_out), .in1(multiplexer_109_out), .out(multiplexer_78_out), .sel(Sa[3]));
  Multiplexer #(.enable("false")) multiplexer_79 (
    .in0(multiplexer_77_out), .in1(multiplexer_117_out), .out(multiplexer_79_out), .sel(Sa[3]));
  Multiplexer #(.enable("false")) multiplexer_80 (
    .in0(multiplexer_78_out), .in1(multiplexer_94_out), .out(multiplexer_80_out), .sel(Sa[2]));
  Multiplexer #(.enable("false")) multiplexer_81 (
    .in0(multiplexer_79_out), .in1(multiplexer_103_out), .out(multiplexer_81_out), .sel(Sa[2]));
  Multiplexer #(.enable("false")) multiplexer_82 (
    .in0(multiplexer_81_out), .in1(multiplexer_95_out), .out(multiplexer_82_out), .sel(Sa[1]));
  Multiplexer #(.enable("false")) multiplexer_83 (
    .in0(multiplexer_80_out), .in1(multiplexer_89_out), .out(multiplexer_83_out), .sel(Sa[1]));
  Multiplexer #(.enable("false")) multiplexer_84 (
    .in0(multiplexer_83_out), .in1(multiplexer_82_out), .out(C[16]), .sel(Sa[0]));
  Multiplexer #(.enable("false")) multiplexer_85 (.in0(B[14]), .in1(Cin), .out(multiplexer_85_out), .sel(Sa[4]));
  Multiplexer #(.enable("false")) multiplexer_86 (.in0(B[13]), .in1(Cin), .out(multiplexer_86_out), .sel(Sa[4]));
  Multiplexer #(.enable("false")) multiplexer_87 (
    .in0(multiplexer_85_out), .in1(multiplexer_125_out), .out(multiplexer_87_out), .sel(Sa[3]));
  Multiplexer #(.enable("false")) multiplexer_88 (
    .in0(multiplexer_86_out), .in1(multiplexer_126_out), .out(multiplexer_88_out), .sel(Sa[3]));
  Multiplexer #(.enable("false")) multiplexer_89 (
    .in0(multiplexer_87_out), .in1(multiplexer_104_out), .out(multiplexer_89_out), .sel(Sa[2]));
  Multiplexer #(.enable("false")) multiplexer_90 (
    .in0(multiplexer_89_out), .in1(multiplexer_96_out), .out(multiplexer_90_out), .sel(Sa[1]));
  Multiplexer #(.enable("false")) multiplexer_91 (
    .in0(multiplexer_82_out), .in1(multiplexer_90_out), .out(C[15]), .sel(Sa[0]));
  Multiplexer #(.enable("false")) multiplexer_92 (
    .in0(multiplexer_90_out), .in1(multiplexer_97_out), .out(C[14]), .sel(Sa[0]));
  Multiplexer #(.enable("false")) multiplexer_93 (.in0(B[12]), .in1(Cin), .out(multiplexer_93_out), .sel(Sa[4]));
  Multiplexer #(.enable("false")) multiplexer_94 (
    .in0(multiplexer_93_out), .in1(multiplexer_133_out), .out(multiplexer_94_out), .sel(Sa[3]));
  Multiplexer #(.enable("false")) multiplexer_95 (
    .in0(multiplexer_88_out), .in1(multiplexer_111_out), .out(multiplexer_95_out), .sel(Sa[2]));
  Multiplexer #(.enable("false")) multiplexer_96 (
    .in0(multiplexer_94_out), .in1(multiplexer_118_out), .out(multiplexer_96_out), .sel(Sa[2]));
  Multiplexer #(.enable("false")) multiplexer_97 (
    .in0(multiplexer_95_out), .in1(multiplexer_105_out), .out(multiplexer_97_out), .sel(Sa[1]));
  Multiplexer #(.enable("false")) multiplexer_98 (
    .in0(multiplexer_96_out), .in1(multiplexer_106_out), .out(multiplexer_98_out), .sel(Sa[1]));
  Multiplexer #(.enable("false")) multiplexer_99 (
    .in0(multiplexer_97_out), .in1(multiplexer_98_out), .out(C[13]), .sel(Sa[0]));
  Multiplexer #(.enable("false")) multiplexer_100 (
    .in0(multiplexer_98_out), .in1(multiplexer_107_out), .out(C[12]), .sel(Sa[0]));
  Multiplexer #(.enable("false")) multiplexer_101 (.in0(B[10]), .in1(Cin), .out(multiplexer_101_out), .sel(Sa[4]));
  Multiplexer #(.enable("false")) multiplexer_102 (.in0(B[11]), .in1(Cin), .out(multiplexer_102_out), .sel(Sa[4]));
  Multiplexer #(.enable("false")) multiplexer_103 (
    .in0(multiplexer_102_out), .in1(multiplexer_142_out), .out(multiplexer_103_out), .sel(Sa[3]));
  Multiplexer #(.enable("false")) multiplexer_104 (
    .in0(multiplexer_101_out), .in1(multiplexer_141_out), .out(multiplexer_104_out), .sel(Sa[3]));
  Multiplexer #(.enable("false")) multiplexer_105 (
    .in0(multiplexer_103_out), .in1(multiplexer_119_out), .out(multiplexer_105_out), .sel(Sa[2]));
  Multiplexer #(.enable("false")) multiplexer_106 (
    .in0(multiplexer_104_out), .in1(multiplexer_128_out), .out(multiplexer_106_out), .sel(Sa[2]));
  Multiplexer #(.enable("false")) multiplexer_107 (
    .in0(multiplexer_105_out), .in1(multiplexer_112_out), .out(multiplexer_107_out), .sel(Sa[1]));
  Multiplexer #(.enable("false")) multiplexer_108 (
    .in0(multiplexer_107_out), .in1(multiplexer_113_out), .out(C[11]), .sel(Sa[0]));
  Multiplexer #(.enable("false")) multiplexer_109 (.in0(B[8]), .in1(Cin), .out(multiplexer_109_out), .sel(Sa[4]));
  Multiplexer #(.enable("false")) multiplexer_110 (.in0(B[9]), .in1(Cin), .out(multiplexer_110_out), .sel(Sa[4]));
  Multiplexer #(.enable("false")) multiplexer_111 (
    .in0(multiplexer_110_out), .in1(multiplexer_149_out), .out(multiplexer_111_out), .sel(Sa[3]));
  Multiplexer #(.enable("false")) multiplexer_112 (
    .in0(multiplexer_111_out), .in1(multiplexer_127_out), .out(multiplexer_112_out), .sel(Sa[2]));
  Multiplexer #(.enable("false")) multiplexer_113 (
    .in0(multiplexer_106_out), .in1(multiplexer_121_out), .out(multiplexer_113_out), .sel(Sa[1]));
  Multiplexer #(.enable("false")) multiplexer_114 (
    .in0(multiplexer_112_out), .in1(multiplexer_120_out), .out(multiplexer_114_out), .sel(Sa[1]));
  Multiplexer #(.enable("false")) multiplexer_115 (
    .in0(multiplexer_113_out), .in1(multiplexer_114_out), .out(C[10]), .sel(Sa[0]));
  Multiplexer #(.enable("false")) multiplexer_116 (
    .in0(multiplexer_114_out), .in1(multiplexer_122_out), .out(C[9]), .sel(Sa[0]));
  Multiplexer #(.enable("false")) multiplexer_117 (.in0(B[7]), .in1(Cin), .out(multiplexer_117_out), .sel(Sa[4]));
  Multiplexer #(.enable("false")) multiplexer_118 (
    .in0(multiplexer_109_out), .in1(multiplexer_150_out), .out(multiplexer_118_out), .sel(Sa[3]));
  Multiplexer #(.enable("false")) multiplexer_119 (
    .in0(multiplexer_117_out), .in1(Cin), .out(multiplexer_119_out), .sel(Sa[3]));
  Multiplexer #(.enable("false")) multiplexer_120 (
    .in0(multiplexer_119_out), .in1(multiplexer_143_out), .out(multiplexer_120_out), .sel(Sa[2]));
  Multiplexer #(.enable("false")) multiplexer_121 (
    .in0(multiplexer_118_out), .in1(multiplexer_134_out), .out(multiplexer_121_out), .sel(Sa[2]));
  Multiplexer #(.enable("false")) multiplexer_122 (
    .in0(multiplexer_121_out), .in1(multiplexer_129_out), .out(multiplexer_122_out), .sel(Sa[1]));
  Multiplexer #(.enable("false")) multiplexer_123 (
    .in0(multiplexer_120_out), .in1(multiplexer_136_out), .out(multiplexer_123_out), .sel(Sa[1]));
  Multiplexer #(.enable("false")) multiplexer_124 (
    .in0(multiplexer_122_out), .in1(multiplexer_123_out), .out(C[8]), .sel(Sa[0]));
  Multiplexer #(.enable("false")) multiplexer_125 (.in0(B[6]), .in1(Cin), .out(multiplexer_125_out), .sel(Sa[4]));
  Multiplexer #(.enable("false")) multiplexer_126 (.in0(B[5]), .in1(Cin), .out(multiplexer_126_out), .sel(Sa[4]));
  Multiplexer #(.enable("false")) multiplexer_127 (
    .in0(multiplexer_126_out), .in1(Cin), .out(multiplexer_127_out), .sel(Sa[3]));
  Multiplexer #(.enable("false")) multiplexer_128 (
    .in0(multiplexer_125_out), .in1(Cin), .out(multiplexer_128_out), .sel(Sa[3]));
  Multiplexer #(.enable("false")) multiplexer_129 (
    .in0(multiplexer_128_out), .in1(multiplexer_144_out), .out(multiplexer_129_out), .sel(Sa[2]));
  Multiplexer #(.enable("false")) multiplexer_130 (
    .in0(multiplexer_129_out), .in1(multiplexer_135_out), .out(multiplexer_130_out), .sel(Sa[1]));
  Multiplexer #(.enable("false")) multiplexer_131 (
    .in0(multiplexer_123_out), .in1(multiplexer_130_out), .out(C[7]), .sel(Sa[0]));
  Multiplexer #(.enable("false")) multiplexer_132 (
    .in0(multiplexer_130_out), .in1(multiplexer_137_out), .out(C[6]), .sel(Sa[0]));
  Multiplexer #(.enable("false")) multiplexer_133 (.in0(B[4]), .in1(Cin), .out(multiplexer_133_out), .sel(Sa[4]));
  Multiplexer #(.enable("false")) multiplexer_134 (
    .in0(multiplexer_133_out), .in1(Cin), .out(multiplexer_134_out), .sel(Sa[3]));
  Multiplexer #(.enable("false")) multiplexer_135 (
    .in0(multiplexer_134_out), .in1(multiplexer_157_out), .out(multiplexer_135_out), .sel(Sa[2]));
  Multiplexer #(.enable("false")) multiplexer_136 (
    .in0(multiplexer_127_out), .in1(multiplexer_151_out), .out(multiplexer_136_out), .sel(Sa[2]));
  Multiplexer #(.enable("false")) multiplexer_137 (
    .in0(multiplexer_136_out), .in1(multiplexer_146_out), .out(multiplexer_137_out), .sel(Sa[1]));
  Multiplexer #(.enable("false")) multiplexer_138 (
    .in0(multiplexer_135_out), .in1(multiplexer_145_out), .out(multiplexer_138_out), .sel(Sa[1]));
  Multiplexer #(.enable("false")) multiplexer_139 (
    .in0(multiplexer_138_out), .in1(multiplexer_147_out), .out(C[4]), .sel(Sa[0]));
  Multiplexer #(.enable("false")) multiplexer_140 (
    .in0(multiplexer_137_out), .in1(multiplexer_138_out), .out(C[5]), .sel(Sa[0]));
  Multiplexer #(.enable("false")) multiplexer_141 (.in0(B[2]), .in1(Cin), .out(multiplexer_141_out), .sel(Sa[4]));
  Multiplexer #(.enable("false")) multiplexer_142 (.in0(B[3]), .in1(Cin), .out(multiplexer_142_out), .sel(Sa[4]));
  Multiplexer #(.enable("false")) multiplexer_143 (
    .in0(multiplexer_142_out), .in1(Cin), .out(multiplexer_143_out), .sel(Sa[3]));
  Multiplexer #(.enable("false")) multiplexer_144 (
    .in0(multiplexer_141_out), .in1(Cin), .out(multiplexer_144_out), .sel(Sa[3]));
  Multiplexer #(.enable("false")) multiplexer_145 (
    .in0(multiplexer_144_out), .in1(Cin), .out(multiplexer_145_out), .sel(Sa[2]));
  Multiplexer #(.enable("false")) multiplexer_146 (
    .in0(multiplexer_143_out), .in1(Cin), .out(multiplexer_146_out), .sel(Sa[2]));
  Multiplexer #(.enable("false")) multiplexer_147 (
    .in0(multiplexer_146_out), .in1(multiplexer_152_out), .out(multiplexer_147_out), .sel(Sa[1]));
  Multiplexer #(.enable("false")) multiplexer_148 (
    .in0(multiplexer_147_out), .in1(multiplexer_153_out), .out(C[3]), .sel(Sa[0]));
  Multiplexer #(.enable("false")) multiplexer_149 (.in0(B[1]), .in1(Cin), .out(multiplexer_149_out), .sel(Sa[4]));
  Multiplexer #(.enable("false")) multiplexer_150 (.in0(B[0]), .in1(Cin), .out(multiplexer_150_out), .sel(Sa[4]));
  Multiplexer #(.enable("false")) multiplexer_151 (
    .in0(multiplexer_149_out), .in1(Cin), .out(multiplexer_151_out), .sel(Sa[3]));
  Multiplexer #(.enable("false")) multiplexer_152 (
    .in0(multiplexer_151_out), .in1(Cin), .out(multiplexer_152_out), .sel(Sa[2]));
  Multiplexer #(.enable("false")) multiplexer_153 (
    .in0(multiplexer_145_out), .in1(multiplexer_158_out), .out(multiplexer_153_out), .sel(Sa[1]));
  Multiplexer #(.enable("false")) multiplexer_154 (
    .in0(multiplexer_152_out), .in1(Cin), .out(multiplexer_154_out), .sel(Sa[1]));
  Multiplexer #(.enable("false")) multiplexer_155 (
    .in0(multiplexer_153_out), .in1(multiplexer_154_out), .out(C[2]), .sel(Sa[0]));
  Multiplexer #(.enable("false")) multiplexer_156 (
    .in0(multiplexer_154_out), .in1(multiplexer_159_out), .out(C[1]), .sel(Sa[0]));
  Multiplexer #(.enable("false")) multiplexer_157 (
    .in0(multiplexer_150_out), .in1(Cin), .out(multiplexer_157_out), .sel(Sa[3]));
  Multiplexer #(.enable("false")) multiplexer_158 (
    .in0(multiplexer_157_out), .in1(Cin), .out(multiplexer_158_out), .sel(Sa[2]));
  Multiplexer #(.enable("false")) multiplexer_159 (
    .in0(multiplexer_158_out), .in1(Cin), .out(multiplexer_159_out), .sel(Sa[1]));
  Multiplexer #(.enable("false")) multiplexer_160 (.in0(multiplexer_159_out), .in1(Cin), .out(C[0]), .sel(Sa[0]));
endmodule
